# Fritzing sketch AutonomousCar (saved by Fritzing 0.9.3b)
breadboards: 2

parts:
  U1 = ESP32S-HiLetgo [part_number=ESP32S-HiLetgo]
  U2 = OV7670 Camera [package=camera_sfv24r-2st_2]
  Part1 = Arduino Nano 33 BLE Sense
  hc-sr1 = hc-sr04
  hc-sr2 = hc-sr04
  hc-sr3 = hc-sr04
  BAT1 = Battery Holders [package=lipo-1100mAh]
  L298N1 = L298N DC motor driver
  M1 = MT3608 Module
  M2 = DC Motor  # not connected
  M3 = DC Motor  # not connected
  Part2 = Passive Buzzer
  T1 = LM35 Temperature Sensor [package="TO92 [THT]"]

nets:
  N1: U1.GPIO34, T1.Vout
  N2: U1.GPIO35, hc-sr3.Echo
  N3: U1.GPIO32, L298N1.IN2
  N4: U1.GPIO33, hc-sr3.Trig
  N5: U1.GPIO26, hc-sr2.Trig
  N6: U1.GPIO27, hc-sr2.Echo
  N7: U1.GPIO14, L298N1.ENA
  GND: U1.GND, hc-sr1.GND, hc-sr2.GND, hc-sr3.GND, BAT1.-, M1.pin1, M1.pin2, Part2.GND, T1.GND
  N8: U1.GPIO13, L298N1.IN1
  VCC: U1.VIN, U2.3V3, Part1.VIN, Part1.3V3, hc-sr1.VCC, hc-sr2.VCC, hc-sr3.VCC, BAT1.+, Part2.NC, T1.+Vs
  N9: U1.GPIO7, hc-sr1.Trig
  N10: U1.GPIO8, hc-sr1.Echo
  N11: U1.GPIO4, Part2.S
  N12: U1.GPIO16, Part1.D11/MOSI, Part1.+5V
  N13: U1.GPIO17, Part1.D7
  N14: U1.GPIO5, L298N1.IN4
  N15: U1.GPIO18, L298N1.ENB
  N16: U1.GPIO23, L298N1.IN3
  N17: U2.SIOC, Part1.A5
  N18: U2.VSYNC, Part1.D8
  N19: U2.PCLK, Part1.A0
  N20: U2.D7, Part1.D4
  N21: U2.D5, Part1.D5~
  N22: U2.D3, Part1.D2
  N23: U2.D1, Part1.D10~
  N24: U2.RESET, Part1.A2
  GND_2: U2.GND, Part1.GND, Part1.A7
  N25: U2.SIDO, Part1.A4
  N26: U2.HREF, Part1.A1
  N27: U2.XCLK, Part1.D9~
  N28: U2.D6, Part1.D6~
  N29: U2.D4, Part1.D3~
  N30: U2.D0, Part1.TX
  N31: U2.PWDN, Part1.A3
  N32: L298N1.12V, M1.pin3
  N33: L298N1.GND, M1.pin4

custom parts:
  ESP32S-HiLetgo: HiLetgo ESP-WROOM-32 ESP32 ESP-32S Development Board 2.4GHz Dual-Mode WiFi + Bluetooth Dual Cores Microcontroller The ESP32 integrated with Antenna switches, RF Balun, power amplifiers, low-noise amplifiers, filters, and management modules, and the entire solution occupies the least area of PCB. 2.4 GHz Wi-Fi plus Bluetooth dual-mode chip, with TSMC Ultra-low power consumption 40nm technology,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
  OV7670 Camera: CMOS image sensor
  Arduino Nano 33 BLE Sense: The Nano 33 BLE Sense (without headers) is Arduino’s 3.3V AI enabled board in the smallest available form factor: 45x18mm! The Arduino Nano 33 BLE Sense is a completely new board on a well-known form factor. It comes with a series of embedded sensors: 9 axis inertial sensor: what makes this board ideal for wearable devices humidity, and temperature sensor: to get highly accurate measurements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
  L298N DC motor driver: 2x DC motor driver with 78M05 positive voltage regulator (7..35 V) L298N: max 46 V, 2 A Set 5 V Enable jumper to enable 5 V regultor (needed for the L298N) and +5 V output at screw terminal or supply external +5 V at screw terminal Set ENA and/or ENB to +5 V to enable motor permanently or supply ENA and/or ENB with PWM signal IN1 and IN2 set rotation directory for motor A (OUT1/OUT2) IN2 and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
  MT3608 Module: MT3608 Boost Converter Module Links: Aerosemi MT3608 2A Step Up Converter datasheet
